# Fritzing sketch BasicClock (saved by Fritzing 0.9.6b)
breadboards: 1

parts:
  A1 = Raspberry Pi Pico W
  Part1 = LCD1602-I2C

nets:
  N1: A1.pin_3, A1.pin_8, A1.pin_13, A1.pin_18, A1.pin_23, A1.pin_28, A1.pin_33, A1.pin_38, Part1.GND
  N2: A1.pin_19, Part1.SDA
  N3: A1.pin_20, Part1.SCL
  N4: A1.pin_40, Part1.VCC

custom parts:
  Raspberry Pi Pico W: Raspberry Pi Pico W. Based around the RP2040 microcontroller the Pico W is a low cost microcontroller device bringing Raspberry Pi quality, cost, and easy of use to the microcontroller space. The areas marked KEEPOUT in pcb silkscreen should not have traces running through them to avoid shorts on a soldered in module!
  LCD1602-I2C: A standard character display, usually with 2x16 characters. Comes in many colors with LCM1602 IIC attached.
