# Fritzing sketch StepperClock (saved by Fritzing 0.9.6b)
breadboards: 1

parts:
  A1 = Raspberry Pi Pico W
  Driver1 = 28BYJ-48 Driver Module [part_number=ULN2003 package=THT]
  SM1 = 28BYJ-48 Stepper Motor [part_number=28BYJ-48]
  LED1 = LED - 5mm [color="Infrared (940nm)" current=0.030 package="5 mm [THT]"]
  Q1 = LTR-301 [package=ltr-301]
  R1 = Resistor [tolerance=±5% power=0.25 resistance=1M package=THT]  # not connected
  R2 = Resistor [tolerance=±5% power=0.25 resistance=67 package=THT]  # not connected

nets:
  N1: A1.pin_3, A1.pin_8, A1.pin_13, A1.pin_18, A1.pin_23, A1.pin_28, A1.pin_33, A1.pin_38, A1.pin_42, Driver1.GND, LED1.cathode, Q1.E
  N2: A1.pin_14, Driver1.IN4
  N3: A1.pin_15, Driver1.IN3
  N4: A1.pin_16, Driver1.IN2
  N5: A1.pin_17, Driver1.IN1
  N6: A1.pin_21, A1.pin_36
  N7: A1.pin_40, Driver1.Vmotor
  N8: Driver1.blue-pin, SM1.blue-pin
  N9: Driver1.pink-pin, SM1.pink-pin
  N10: Driver1.yellow-pin, SM1.yellow-pin
  N11: Driver1.orange-pin, SM1.orange-pin
  N12: Driver1.red-pin, SM1.red-pin

custom parts:
  Raspberry Pi Pico W: Raspberry Pi Pico W. Based around the RP2040 microcontroller the Pico W is a low cost microcontroller device bringing Raspberry Pi quality, cost, and easy of use to the microcontroller space. The areas marked KEEPOUT in pcb silkscreen should not have traces running through them to avoid shorts on a soldered in module!
  28BYJ-48 Driver Module: ULN2003 Driver Module for the 28BYJ-48 Unipolar Stepper Motor LED A - Blue wire - Bottom coil left LED B - Pink wire - Top coil left LED C - Yellow wire - Bottom coil right LED D - Orange wire - Top coil right Common rail - red Connector pins: blue - pink - yellow - orange - red Control pins - IN1 to IN4 Power pins - GND & Vmotor (5-12V) On/Off jumper (if removed, power to motor is cut).
  28BYJ-48 Stepper Motor: Unipolar Stepper Motor 28BYJ-48 Top coil - pink & orange Bottom coil - blue & yellow Common rail - red Connector pins: blue - pink - yellow - orange - red
